# Fritzing sketch Security-Breadboard (saved by Fritzing 0.9.2b)
circuit board: 8.67406cm x 8.20733cm
breadboards: 1

parts:
  USB_Power_in = USB Connectors [package=usb-a-h]
  Adafruit_PIR = PIR sensor
  Q1 = TRANSISTOR_NPN [package=to-92]
  R1 = Resistor [tolerance=±5% resistance=1k package=THT]
  Speaker = SPEAKER [package=pcb_mount_speaker]
  J1 = Screw terminal - 2 pins [package=THT]
  J2 = Screw terminal - 2 pins [package=THT]
  J3 = Screw terminal - 2 pins [package=THT]
  J5 = Screw terminal - 2 pins [package=THT]
  J6 = Screw terminal - 2 pins [package=THT]
  J7 = Screw terminal - 2 pins [package=THT]
  RelayModule_DFR0017_V3_1 = RelayModule DFR0017 V3.1
  TSL2561 = Adafruit TSL2561 [package="SIP (Single Inline) [THT]"]
  S1 = Pushbutton [package="[THT]"]
  R2 = Resistor [tolerance=±5% resistance=10k package=THT]
  C1 = Electrolytic Capacitor [capacitance=0.1mF package="100 mil [THT, electrolytic]"]
  C2 = Ceramic Capacitor [capacitance=100nF package="100 mil [THT, multilayer]"]
  R5 = Resistor [tolerance=±5% resistance=56k package=THT]
  R6 = Resistor [tolerance=±5% resistance=100k package=THT]
  R7 = Resistor [tolerance=±5% resistance=470k package=THT]
  R8 = Resistor [tolerance=±5% resistance=470k package=THT]
  LDR1 = Photocell (LDR) [package=THT]
  Adafruit_HUZZAH_ESP8266_Breakout1 = Adafruit HUZZAH ESP8266 Breakout [part_number=2471]

nets:
  5V: USB_Power_in.VBUS, Adafruit_PIR.VDD, Speaker.-, J3.pin1, J5.pin1, J6.pin1, RelayModule_DFR0017_V3_1.5V, C1.+, C2.0, Adafruit_HUZZAH_ESP8266_Breakout1.VBat
  GND: USB_Power_in.GND, Adafruit_PIR.GND, Q1.E, J1.pin1, J5.pin2, J6.pin2, RelayModule_DFR0017_V3_1.GND, TSL2561.GND, R2.Pin_1, C1.-, C2.1, R5.Pin_1, R7.Pin_1, R8.Pin_1, Adafruit_HUZZAH_ESP8266_Breakout1.GND
  PIR_Signal: Adafruit_PIR.SIG, J2.pin1, Adafruit_HUZZAH_ESP8266_Breakout1.#4
  N1: Q1.B, R1.Pin_0
  Alarm_Spk: Q1.C, Speaker.+, J3.pin2
  Alarm_Out: R1.Pin_1, Adafruit_HUZZAH_ESP8266_Breakout1.#15
  3.3V: J1.pin2, TSL2561.Vin, S1.Pin_1, S1.Pin_2, R6.Pin_0, Adafruit_HUZZAH_ESP8266_Breakout1.3V
  SCL_Light: J7.pin1, TSL2561.SCL, Adafruit_HUZZAH_ESP8266_Breakout1.#12
  SDA_Light: J7.pin2, TSL2561.SDA, Adafruit_HUZZAH_ESP8266_Breakout1.#13
  Relay_On: RelayModule_DFR0017_V3_1.SIGNAL, Adafruit_HUZZAH_ESP8266_Breakout1.#5
  N2: S1.Pin_3, S1.Pin_4, R2.Pin_0, Adafruit_HUZZAH_ESP8266_Breakout1.#14
  N3: R5.Pin_0, LDR1.pin_1, Adafruit_HUZZAH_ESP8266_Breakout1.A
  N4: R6.Pin_1, R7.Pin_0, R8.Pin_0, LDR1.pin_0
  N5: Adafruit_HUZZAH_ESP8266_Breakout1.#16, Adafruit_HUZZAH_ESP8266_Breakout1.RST

notes:
  VCC in
  PIR
  TSL2561
  Speaker
  - +
  - +   in
  + - SDA SCL
  ----------------------------------------------
  The area below the doted line is not on the
  final PCB. Everything below the dotted line
  is placed outside the PCB!

custom parts:
  Adafruit TSL2561: Adafruit TSL2561 Digital Luminosity/Lux/Light Sensor Breakout The TSL2561 luminosity sensor is an advanced digital light sensor, ideal for use in a wide range of light situations. Compared to low cost CdS cells, this sensor is more precise, allowing for exact lux calculations and can be configured for different gain/timing ranges to detect light ranges from up to 0.1 - 40,000+ Lux on the fly.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
