# Fritzing sketch Security-Simple (saved by Fritzing 0.9.2b)
circuit board: 8cm x 5.5cm
breadboards: 1

parts:
  USB_Power_in = USB Connectors [package=usb-a-h]
  Adafruit_PIR = PIR sensor
  Q1 = TRANSISTOR_NPN [package=to-92]
  R1 = Resistor [tolerance=±5% resistance=1k package=THT]
  Relay_DFR0017_V3_1 = RelayModule DFR0017 V3.1
  C1 = Electrolytic Capacitor [capacitance=0.1mF package="100 mil [THT, electrolytic]"]
  C2 = Ceramic Capacitor [capacitance=100nF package="100 mil [THT, multilayer]"]
  R5 = Resistor [tolerance=±5% resistance=56k package=THT]
  R6 = Resistor [tolerance=±5% resistance=100k package=THT]
  R7 = Resistor [tolerance=±5% resistance=470k package=THT]
  R8 = Resistor [tolerance=±5% resistance=470k package=THT]
  LDR1 = Photocell (LDR) [package=THT]
  Adafruit_HUZZAH_ESP8266 = Adafruit HUZZAH ESP8266 Breakout [part_number=2471]
  Speaker = Piezo Speaker

nets:
  5V: USB_Power_in.VBUS, Adafruit_PIR.VDD, Relay_DFR0017_V3_1.5V, C1.+, C2.0, Adafruit_HUZZAH_ESP8266.VBat, Speaker.pin2
  GND: USB_Power_in.GND, Adafruit_PIR.GND, Q1.E, Relay_DFR0017_V3_1.GND, C1.-, C2.1, R5.Pin_1, R7.Pin_1, R8.Pin_1, Adafruit_HUZZAH_ESP8266.GND
  PIR_Signal: Adafruit_PIR.SIG, Adafruit_HUZZAH_ESP8266.#4
  N1: Q1.B, R1.Pin_0
  Alarm_Spk: Q1.C, Speaker.pin1
  Alarm_Out: R1.Pin_1, Adafruit_HUZZAH_ESP8266.#15
  Relay_On: Relay_DFR0017_V3_1.SIGNAL, Adafruit_HUZZAH_ESP8266.#5
  N2: R5.Pin_0, LDR1.pin_1, Adafruit_HUZZAH_ESP8266.A
  3.3V: R6.Pin_0, Adafruit_HUZZAH_ESP8266.3V
  N3: R6.Pin_1, R7.Pin_0, R8.Pin_0, LDR1.pin_0
  N4: Adafruit_HUZZAH_ESP8266.#16, Adafruit_HUZZAH_ESP8266.RST

notes:
  ESP8266 backyard auto light, 1.0
  Relay
  GND
  5V
  SIG
  SND
  RST
  A
  16
  3.3V
  15
  5
  4
  +
  -
