# Fritzing sketch Security (saved by Fritzing 0.9.2b)
circuit board: 8.67406cm x 8.20733cm
breadboards: 1

parts:
  Adafruit_HUZZAH_ESP8266_Breakout1 = Adafruit HUZZAH ESP8266 Breakout [part_number=2471]
  USB_Power_in = USB Connectors [package=usb-a-h]
  Adafruit_PIR = PIR sensor
  Q1 = TRANSISTOR_NPN [package=to-92]
  R1 = Resistor [tolerance=±5% resistance=1k package=THT]
  Speaker = SPEAKER [package=pcb_mount_speaker]
  Adafruit_TSL2561 = _TL2561
  J1 = Screw terminal - 2 pins [package=THT]
  J2 = Screw terminal - 2 pins [package=THT]
  J3 = Screw terminal - 2 pins [package=THT]
  J5 = Screw terminal - 2 pins [package=THT]
  J6 = Screw terminal - 2 pins [package=THT]
  J7 = Screw terminal - 2 pins [package=THT]
  RelayModule_DFR1 = RelayModule DFR0017

nets:
  GND: Adafruit_HUZZAH_ESP8266_Breakout1.GND, USB_Power_in.GND, Adafruit_PIR.GND, Q1.E, Adafruit_TSL2561.GND, J1.pin1, J5.pin2, J6.pin2, RelayModule_DFR1.GND
  5V: Adafruit_HUZZAH_ESP8266_Breakout1.VBat, USB_Power_in.VBUS, Adafruit_PIR.VDD, Speaker.-, J3.pin1, J5.pin1, J6.pin1, RelayModule_DFR1.5V
  SDA_Light: Adafruit_HUZZAH_ESP8266_Breakout1.#13, Adafruit_TSL2561.SDA, J7.pin2
  SCL_Light: Adafruit_HUZZAH_ESP8266_Breakout1.#12, Adafruit_TSL2561.SCL, J7.pin1
  R_Signal: Adafruit_HUZZAH_ESP8266_Breakout1.#5, RelayModule_DFR1.SIGNAL
  PIR_Signal: Adafruit_HUZZAH_ESP8266_Breakout1.#4, Adafruit_PIR.SIG, J2.pin1
  Alarm_Out: Adafruit_HUZZAH_ESP8266_Breakout1.#15, R1.Pin_1
  N1: Adafruit_HUZZAH_ESP8266_Breakout1.3V, Adafruit_TSL2561.Vcc, J1.pin2
  N2: Q1.B, R1.Pin_0
  Alarm_Spk: Q1.C, Speaker.+, J3.pin2

notes:
  Old board version, new board has different connector!!!!!
  VCC in
  PIR
  TSL2561
  Speaker
  - +
  - +   in
  + - SDA SCL
  ----------------------------------------------

custom parts:
  : Sensor de Luminosidade - TL2561
